// Digital circuit circuit.dig as structural Verilog
module circuit (
  input  in_1,
  input  in_2,
  input  SHCP,
  input  STCP,
  input  SCLR,
  input  DS,
  input  SHCP_2,
  input  STCP_2,
  input  SCLR_2,
  input  DS_2,
  input  SHCP_3,
  input  STCP_3,
  input  SCLR_3,
  input  DS_3,
  output out_3,
  output out_4,
  output QA,
  output QB,
  output QC,
  output QD,
  output QA_2,
  output QB_2,
  output QC_2,
  output QD_2
);

  wire not_1_out, not_2_out, not_3_out, not_4_out, not_5_out;

  not not_1 (not_1_out, in_1);
  not not_2 (not_2_out, SCLR_2);
  JK_FF jk_ff_1 (.J(not_2_out), .C(STCP_2), .K(SCLR_2));  // open: Q, nQ
  JK_FF jk_ff_2 ();  // open: J, C, K, Q, nQ
  RS_FF rs_ff_1 (.S(in_1), .C(in_2), .R(not_1_out), .Q(out_3), .nQ(out_4));
  D_FF d_ff_1 (.C(STCP), .Q(QA));  // open: D, nQ
  D_FF d_ff_2 (.C(STCP), .Q(QB));  // open: D, nQ
  D_FF d_ff_3 (.C(STCP), .Q(QC));  // open: D, nQ
  D_FF d_ff_4 (.C(STCP), .Q(QD));  // open: D, nQ
  not not_3 (not_3_out, SCLR_2);
  JK_FF jk_ff_3 (.J(not_3_out), .C(STCP_2), .K(SCLR_2));  // open: Q, nQ
  JK_FF jk_ff_4 ();  // open: J, C, K, Q, nQ
  not not_4 (not_4_out, SCLR_2);
  JK_FF jk_ff_5 (.J(not_4_out), .C(STCP_2), .K(SCLR_2));  // open: Q, nQ
  JK_FF jk_ff_6 ();  // open: J, C, K, Q, nQ
  not not_5 (not_5_out, SCLR_2);
  JK_FF jk_ff_7 (.J(not_5_out), .C(STCP_2), .K(SCLR_2));  // open: Q, nQ
  JK_FF jk_ff_8 ();  // open: J, C, K, Q, nQ
endmodule
